# Fritzing sketch shangyin-connection (saved by Fritzing 0.9.3b)
circuit board: 8.46667cm x 5.64444cm

parts:
  LCD1 = LCD screen
  Raspberry_Pi_A1 = Raspberry Pi A
  Part1 = RFID-RC522-v3
  J1 = Piezo Speaker  # not connected

nets:
  VDD: LCD1.VDD, LCD1.LED+, Raspberry_Pi_A1.5V
  N1: LCD1.RS, Raspberry_Pi_A1.GPIO_25
  GND: LCD1.R/W, LCD1.LED-, Raspberry_Pi_A1.GND, Part1.GND
  N2: LCD1.E, Raspberry_Pi_A1.GPIO_24
  N3: LCD1.DB4, Raspberry_Pi_A1.GPIO_22
  N4: LCD1.DB5, Raspberry_Pi_A1.GPIO_23
  N5: LCD1.DB6, Raspberry_Pi_A1.GPIO_27
  N6: LCD1.DB7, Raspberry_Pi_A1.GPIO_17
  3V3: Raspberry_Pi_A1.3V3, Part1.3.3V
  N7: Raspberry_Pi_A1.GPIO_14, Part1.IRQ
  N8: Raspberry_Pi_A1.GPIO_15, Part1.RST
  N9: Raspberry_Pi_A1.GPIO_10, Part1.MOSI
  N10: Raspberry_Pi_A1.GPIO_9, Part1.MISO
  N11: Raspberry_Pi_A1.GPIO_11, Part1.SCK
  N12: Raspberry_Pi_A1.GPIO_8, Part1.SDA

custom parts:
  RFID-RC522-v3: A simple China made RFID-RC522 Reader (6x4 cm); do check the pin labels, as this is a MFRC522 based clone.
